// Logisim project mips-single.circ as structural Verilog: 9 circuits, main circuit MIPS
module MIPS (
  output [31:0] out_1,
  output [31:0] out_2,
  output [31:0] out_3,
  output [31:0] out_4,
  output [31:0] out_5
);

  wire A0, A1, A2, A3, A4, A5, and_1_out, C0, C1, C2, C3, C4, C5, C6, Clk, M0, M1, M2, M3, M4, or_1_out,
       pre_alucontrol_1_isfunct, Rs;
  wire [0:0] comparator_1_lt, comparator_2_lt;
  wire [3:0] mips_alu_1_p3, multiplexer_10_out, shifter_2_out;
  wire [4:0] mips_alu_1_p4, multiplexer_1_out, multiplexer_2_out;
  wire [5:0] pre_alucontrol_1_realop;
  wire [23:0] bit_extender_2_out;
  wire [25:0] PC4;
  wire [29:0] BRN, multiplexer_11_out, multiplexer_12_out, PC, register_1_q;
  wire [29:26] JUM;
  wire [31:0] FD, load_byte_shifter_1_dataout, mips_alu_1_p5, mips_ram_1_p8, multiplexer_3_out,
       multiplexer_4_out, multiplexer_5_out, multiplexer_7_out, multiplexer_13_out, multiplexer_15_out,
       shifter_1_out, WB;

  Clock clock_1 (.out(Clk));
  Button button_1 (.out(Rs));
  Register #(.width(30)) register_1 (.D(PC), .en(1'b1), .clk(Clk), .Q(register_1_q), .clr(Rs));
  // Incrementer #(.width(30)) incrementer_1: pin names not known; wires that end beside it: register_1_q, {JUM, PC4}, {register_1_q, 2'b00}
  // MIPSProgramROM mipsprogramrom_1: pin names not known; wires that end beside it: FD
  Multiplexer #(.width(5), .enable("false")) multiplexer_1 (
    .in0(FD[20:16]), .in1(FD[15:11]), .out(multiplexer_1_out), .sel(C0));
  Multiplexer #(.width(5), .enable("false")) multiplexer_2 (
    .in0(multiplexer_1_out), .in1({5{1'b1}}), .out(multiplexer_2_out), .sel(C1));
  assign out_5 = {{16{FD[15]}}, FD[15:0]};  // Bit_Extender bit_extender_1
  Control control_1 (
    .Op(FD[31:26]), .RegDst(C0), .IsRetrnAddr(C1), .Jump(C2), .Branch(C3), .MemtoReg(C4), .ALUSrc(C5),
    .IsLUI(C6));
  // RegisterFile registerfile_1: pin names not known; wires that end beside it: WB, Clk, A0, multiplexer_2_out, FD[25:21], FD[20:16], out_1, out_4
  Multiplexer #(.width(32), .enable("false")) multiplexer_3 (
    .in0(out_1), .in1({32{1'b0}}), .out(multiplexer_3_out), .sel(C6));
  Multiplexer #(.width(32), .enable("false")) multiplexer_4 (
    .in0(out_5), .in1(shifter_1_out), .out(multiplexer_4_out), .sel(C6));
  Shifter #(.width(32)) shifter_1 (.in(out_5), .\dist (5'b10000), .out(shifter_1_out));
  Multiplexer #(.width(32), .enable("false")) multiplexer_5 (
    .in0(out_4), .in1(multiplexer_4_out), .out(multiplexer_5_out), .sel(C5));
  Adder #(.width(30)) adder_1 (.a({JUM, PC4}), .b(out_5[29:0]), .out(BRN));  // open: cin, cout
  Comparator #(.width(32), .mode("unsigned")) comparator_1 (
    .a(out_1), .b(multiplexer_5_out), .lt(comparator_1_lt[0]));  // open: gt, eq
  Comparator #(.width(32)) comparator_2 (.a(out_1), .b(multiplexer_5_out), .lt(comparator_2_lt[0]));  // open: gt, eq
  // Mips_ALU mips_alu_1: pin names not known; wires that end beside it: multiplexer_3_out, multiplexer_5_out, mips_alu_1_p3, mips_alu_1_p4, mips_alu_1_p5
  Multiplexer #(.width(5), .enable("false")) multiplexer_6 (
    .in0(FD[10:6]), .in1(out_1[4:0]), .out(mips_alu_1_p4), .sel(A3));
  Pre_ALUControl pre_alucontrol_1 (
    .Op(FD[31:26]), .Funct(FD[5:0]), .IsFunct(pre_alucontrol_1_isfunct), .RealOp(pre_alucontrol_1_realop));
  Multiplexer #(.width(32), .enable("false")) multiplexer_7 (
    .in0(mips_alu_1_p5), .in1({{31{1'b0}}, comparator_2_lt[0]}), .out(multiplexer_7_out), .sel(A5));
  ALUControl alucontrol_1 (
    .IsFunct(pre_alucontrol_1_isfunct), .RealOp(pre_alucontrol_1_realop), .ALUOp(mips_alu_1_p3),
    .IsSignedSLT(A5), .IsUnsignedSLT(A4), .RegShifter(A3), .JumpReg(A2), .PCtoReg(A1), .RegWrite(A0));
  Multiplexer #(.width(32), .enable("false")) multiplexer_8 (
    .in0(multiplexer_7_out), .in1({{31{1'b0}}, comparator_1_lt[0]}), .out(out_2), .sel(A4));
  Shifter #(.width(4)) shifter_2 (.in(4'b0001), .\dist (out_2[1:0]), .out(shifter_2_out));
  Bit_Extender #(.in_width(32), .out_width(24)) bit_extender_2 (.in(out_2), .out(bit_extender_2_out));
  Multiplexer #(.width(32), .enable("false")) multiplexer_9 (
    .in0(out_4), .in1({out_4[7:0], out_4[7:0], out_4[7:0], out_4[7:0]}), .out(out_3), .sel(M4));
  Multiplexer #(.width(4), .enable("false")) multiplexer_10 (
    .in0(4'b1111), .in1(shifter_2_out), .out(multiplexer_10_out), .sel(or_1_out));
  or or_1 (or_1_out, M3, M4);
  MemControl memcontrol_1 (.Op(FD[31:26]), .MemRead(M0), .MemWrite(M1), .IsSignedLB(M2), .LoadByte(M3), .StoreByte(M4));
  // MIPS_RAM #(.addrWidth(24)) mips_ram_1: pin names not known; wires that end beside it: bit_extender_2_out, out_3, M1, multiplexer_10_out, Clk, M0, Rs, mips_ram_1_p8
  Multiplexer #(.width(30), .enable("false")) multiplexer_11 (
    .in0({JUM, PC4}), .in1(BRN), .out(multiplexer_11_out), .sel(and_1_out));
  and and_1 (and_1_out, C3, out_2[0]);
  Multiplexer #(.width(30), .enable("false")) multiplexer_12 (
    .in0(multiplexer_11_out), .in1({JUM, FD[25:0]}), .out(multiplexer_12_out), .sel(C2));
  Load_Byte_Shifter load_byte_shifter_1 (
    .Datain(mips_ram_1_p8), .NumBytes(out_2[1:0]), .isSigned(M2), .Dataout(load_byte_shifter_1_dataout));
  Multiplexer #(.width(32), .enable("false")) multiplexer_13 (
    .in0(mips_ram_1_p8), .in1(load_byte_shifter_1_dataout), .out(multiplexer_13_out), .sel(M3));
  Multiplexer #(.width(30), .enable("false")) multiplexer_14 (
    .in0(multiplexer_12_out), .in1(out_1[31:2]), .out(PC), .sel(A2));
  Multiplexer #(.width(32), .enable("false")) multiplexer_15 (
    .in0(out_2), .in1(multiplexer_13_out), .out(multiplexer_15_out), .sel(C4));
  Multiplexer #(.width(32), .enable("false")) multiplexer_16 (
    .in0(multiplexer_15_out), .in1({JUM, PC4, 2'b00}), .out(WB), .sel(A1));

  // Other names for the same wires on the sheet: RR[31:0] = out_4; PC4[29:26] = JUM; ALUOUT[31:0] = out_2;
  //   OP[5:0] = FD[31:26]; IMM32[31:0] = out_5; FUNCT[5:0] = FD[5:0]; JUM[25:0] = FD[25:0]; SHAMT[4:0] = FD[10:6];
  //   LR[31:0] = out_1

  // Notes on the sheet:
  //   FETCH
  //   contents of mipsprogramrom_1 (hex, n*v repeats v):
  //   table_A:        addiu   $t0, $zero, 1   #$t0 = $zero + 1, $t0($8) = 1   lui     $t1, 32768      #$t1
  //   = 32568 << 16 (add at upper 16 bits), bit31 is 1   slti    $t2, $t1, 0     #$t2 = $t1 < 0 = 1, $t1
  //   is negative if 2's complement because bit31 is 1        sltiu   $t3, $t1, 0     #$t3 = $t1 < 0 = 0,
  //   $t1 is positive if unsigned because bit31 is 1      beq     $t2, $zero, L1  #$t2 == $zero goto L1
  //   (always false) (test not taken)   andi    $t0, $t0, 0     #$t0 = $t0 & 0 = 0      ori     $t0, $t0,
  //   2     #$t0 = $t0 | 2 = 2      xori    $t0, $t0, 2     #$t0 = $t0 ^ 2 = 0      beq     $t0, $zero, L1
  //   #$t0 == $zero goto L1 (true) (test taken)       addiu   $t0, $zero, 1   #not doing this instruction
  //   L1:         sb      $t2, 1($sp)     #store 1 from $t2 to $sp+1 (0x10000001) (store byte)    addiu
  //   $t2, $t2, 384   #$t2 = $t2 + 384 = 385  sb      $t2, 3($sp)     #store 385 from $t2 to $sp+3
  //   (0x10000003) should store only 385-256 = 129 (stored in 1 byte)    sw      $t2, 4($sp)     #store
  //   385 from $t2 to $sp+4 (0x10000004) (store word)  lbu     $t3, 3($sp)     #load byte from $sp+3
  //   (0x10000003) (129 or 0x81)        lb      $t4, 3($sp)     #load byte from $sp+3 (0x10000003) with
  //   sign (0xffffff81)       lw      $t5, 4($sp)     #load word from $sp+4 (0x10000004) (385)        jr
  //   $ra table_B:    addiu   $t1, $zero, 2   #$t1 = $zero + 2        lui     $t2, 16384      #$t2 = 16384
  //   << 16 (add at upper 16 bits), bit30 is 1   sll     $t3, $t2, 1     #$t3 = $t2 << 1 (0x80000000)
  //   srav    $t2, $t3, $t1   #$t2 = $t3 >> $t1 (0xe0000000)  or      $t0, $t0, $t1   #$t0 = $t0 | $t1 = 2
  //   srl     $t0, $t0, 1     #$t0 = $t0 >>> 1 = $t0 / 2 = 1  sllv    $t2, $t2, $t0   #$t2 = $t2 << $t0 =
  //   $t2 << 1 (0xc0000000)       sra     $t2, $t2, 31    #$t2 = $t2 >> 31 = all bits are 1 (0xffffffff)
  //   slt     $t3, $t2, $zero #$t3 = $t2 < $zero = 1, $t2 is negative if 2's complement because bit31 is 1
  //   sltu    $t4, $t2, $zero #$t3 = $t2 < $zero = 0, $t2 is positive if unsigned because all bits is 1
  //   srl     $t2, $t2, 31    #$t2 = $t2 >>> 31 = 1   subu    $t1, $t1, $t2   #$t1 = $t1 - $t2 = 2 - 1 = 1
  //   and     $t0, $t1, $zero #$t0 = $t1 & $zero = 0  bne     $t4, $zero, L2  #$t4 == $zero goto L2
  //   (always false) (test not taken)   xor     $t2, $t2, $t2   #$t2 = $t2 ^ $t2 = 0 (reflexive)
  //   bne     $t3, $zero, L2  #$t3 == $zero goto L2 (true) (test taken)       addu    $t0, $zero, $t1 #not
  //   doing this instruction L2:         nor     $t1, $zero, $zero #$t1 = ~($zero | $zero) = 0xffffffff
  //   (all bit is 1)   jr      $ra main:       addu    $sp, $zero, $zero #init stack pointer   lui
  //   $sp, 4096       #init stack pointer     #lui    $s0, 64         #$s0 = 64 << 16 (at start
  //   instruction 1) for qtSPIM test        addiu   $s0, $s0, 4     #$s0 = $s0 + 4 = 4 (for jump to
  //   instrunction 2)         jalr    $s0             #jump to $s0 (table_A)  addu    $t0, $zero, $zero
  //   jal     table_B exit:   addiu   $v0, $zero, 1   #return         nop
  //   DECODE
  //   EXECUTE
  //   There's single-cycle processor but describe steps like multiple-cycles ones.
  //   MEMORY
endmodule

module Control (
  input  [5:0] Op,
  output RegDst,
  output IsRetrnAddr,
  output Jump,
  output Branch,
  output MemtoReg,
  output ALUSrc,
  output IsLUI
);

  Internal_Control internal_control_1 (
    .OP31(Op[5]), .OP30(Op[4]), .OP29(Op[3]), .OP28(Op[2]), .OP27(Op[1]), .OP26(Op[0]), .RegDst(RegDst),
    .IsRetrnAddr(IsRetrnAddr), .Jump(Jump), .Branch(Branch), .MemtoReg(MemtoReg), .ALUSrc(ALUSrc),
    .IsLUI(IsLUI));
endmodule

module MemControl (
  input  [5:0] Op,
  output MemRead,
  output MemWrite,
  output IsSignedLB,
  output LoadByte,
  output StoreByte
);

  Internal_MemControl internal_memcontrol_1 (
    .OP31(Op[5]), .OP30(Op[4]), .OP29(Op[3]), .OP28(Op[2]), .OP27(Op[1]), .OP26(Op[0]), .MemRead(MemRead),
    .MemWrite(MemWrite), .IsSignedLB(IsSignedLB), .LoadByte(LoadByte), .StoreByte(StoreByte));
endmodule

module ALUControl (
  input  IsFunct,
  input  [5:0] RealOp,
  output [3:0] ALUOp,
  output IsSignedSLT,
  output IsUnsignedSLT,
  output RegShifter,
  output JumpReg,
  output PCtoReg,
  output RegWrite
);

  Internal_ALUControl internal_alucontrol_1 (
    .IsFunct(IsFunct), .OP5(RealOp[5]), .OP4(RealOp[4]), .OP3(RealOp[3]), .OP2(RealOp[2]), .OP1(RealOp[1]),
    .OP0(RealOp[0]), .ALUOp3(ALUOp[3]), .ALUOp2(ALUOp[2]), .ALUOp1(ALUOp[1]), .ALUOp0(ALUOp[0]),
    .IsSignedSLT(IsSignedSLT), .IsUnsignedSLT(IsUnsignedSLT), .RegShifter(RegShifter), .JumpReg(JumpReg),
    .PCtoReg(PCtoReg), .RegWrite(RegWrite));
endmodule

module Pre_ALUControl (
  input  [5:0] Op,
  input  [5:0] Funct,
  output IsFunct,
  output [5:0] RealOp
);

  Comparator #(.width(6), .mode("unsigned")) comparator_1 (.a({6{1'b0}}), .b(Op), .eq(IsFunct));  // open: gt, lt
  Multiplexer #(.width(6), .enable("false")) multiplexer_1 (.in0(Op), .in1(Funct), .out(RealOp), .sel(IsFunct));
endmodule

module Load_Byte_Shifter (
  input  [31:0] Datain,
  input  [1:0] NumBytes,
  input  isSigned,
  output [31:0] Dataout
);

  wire [4:0] shifter_1_out;
  wire [31:0] bit_extender_1_out, bit_extender_2_out, shifter_2_out;

  Shifter #(.width(5)) shifter_1 (.in({3'b000, NumBytes}), .\dist (3'b011), .out(shifter_1_out));
  Shifter #(.width(32), .shift("ar")) shifter_2 (.in(Datain), .\dist (shifter_1_out), .out(shifter_2_out));
  assign bit_extender_1_out = {{24{1'b0}}, shifter_2_out[7:0]};  // Bit_Extender bit_extender_1
  Multiplexer #(.width(32), .enable("false")) multiplexer_1 (
    .in0(bit_extender_1_out), .in1(bit_extender_2_out), .out(Dataout), .sel(isSigned));
  assign bit_extender_2_out = {{24{shifter_2_out[7]}}, shifter_2_out[7:0]};  // Bit_Extender bit_extender_2
endmodule

module Internal_Control (
  input  OP31,
  input  OP30,
  input  OP29,
  input  OP28,
  input  OP27,
  input  OP26,
  output RegDst,
  output IsRetrnAddr,
  output Jump,
  output Branch,
  output MemtoReg,
  output ALUSrc,
  output IsLUI
);

  wire not_1_out, not_2_out, not_3_out, not_4_out, not_5_out, not_6_out, not_7_out, not_8_out;

  not not_1 (not_1_out, OP31);
  not not_2 (not_2_out, OP29);
  not not_3 (not_3_out, OP31);
  not not_4 (not_4_out, OP29);
  not not_5 (not_5_out, OP31);
  not not_6 (not_6_out, OP29);
  not not_7 (not_7_out, OP31);
  not not_8 (not_8_out, OP29);
  or or_1 (ALUSrc, OP29, OP31);
  and and_1 (IsLUI, OP28, OP27, OP26);
  and and_2 (RegDst, not_1_out, not_2_out);
  and and_3 (IsRetrnAddr, not_3_out, not_4_out, OP27);
  and and_4 (Jump, not_5_out, not_6_out, OP27);
  and and_5 (Branch, not_7_out, not_8_out, OP28);

  assign MemtoReg = OP31;
endmodule

module Internal_MemControl (
  input  OP31,
  input  OP30,
  input  OP29,
  input  OP28,
  input  OP27,
  input  OP26,
  output MemRead,
  output MemWrite,
  output IsSignedLB,
  output LoadByte,
  output StoreByte
);

  wire and_4_out, and_5_out, not_1_out, not_2_out, not_3_out, not_4_out, not_5_out, not_6_out, not_7_out,
       not_8_out, not_9_out;

  not not_1 (not_1_out, OP29);
  and and_1 (MemWrite, OP31, OP29);
  not not_2 (not_2_out, OP29);
  not not_3 (not_3_out, OP28);
  not not_4 (not_4_out, OP27);
  not not_5 (not_5_out, OP30);
  not not_6 (not_6_out, OP29);
  not not_7 (not_7_out, OP27);
  not not_8 (not_8_out, OP26);
  not not_9 (not_9_out, OP27);
  and and_2 (MemRead, OP31, not_1_out);
  and and_3 (IsSignedLB, OP31, not_2_out, not_3_out, not_4_out);
  and and_4 (and_4_out, OP31, not_5_out, not_6_out, not_7_out, not_8_out);
  and and_5 (and_5_out, OP31, OP28);
  and and_6 (StoreByte, OP31, OP29, not_9_out);
  or or_1 (LoadByte, and_4_out, and_5_out);
endmodule

module Internal_ALUControl (
  input  IsFunct,
  input  OP5,
  input  OP4,
  input  OP3,
  input  OP2,
  input  OP1,
  input  OP0,
  output ALUOp3,
  output ALUOp2,
  output ALUOp1,
  output ALUOp0,
  output IsSignedSLT,
  output IsUnsignedSLT,
  output RegShifter,
  output JumpReg,
  output PCtoReg,
  output RegWrite
);

  wire and_1_out, and_2_out, and_3_out, and_4_out, and_5_out, and_6_out, and_7_out, and_8_out, and_9_out,
       and_10_out, and_11_out, and_13_out, and_14_out, and_16_out, and_17_out, and_18_out, and_19_out,
       and_20_out, and_21_out, and_22_out, not_1_out, not_2_out, not_3_out, not_4_out, not_5_out, not_6_out,
       not_7_out, not_8_out, not_9_out, not_10_out, not_11_out, not_12_out, not_13_out, not_14_out,
       not_15_out, not_16_out, not_17_out, not_18_out, not_19_out, not_20_out, not_21_out, not_22_out,
       not_23_out, not_24_out, not_25_out, not_26_out, not_27_out, not_28_out, not_29_out, not_30_out,
       not_31_out, not_32_out;

  not not_1 (not_1_out, IsFunct);
  not not_2 (not_2_out, OP5);
  not not_3 (not_3_out, OP0);
  not not_4 (not_4_out, IsFunct);
  not not_5 (not_5_out, OP5);
  not not_6 (not_6_out, OP1);
  not not_7 (not_7_out, OP0);
  not not_8 (not_8_out, IsFunct);
  not not_9 (not_9_out, OP3);
  not not_10 (not_10_out, OP0);
  not not_11 (not_11_out, IsFunct);
  not not_12 (not_12_out, OP2);
  not not_13 (not_13_out, IsFunct);
  not not_14 (not_14_out, OP3);
  not not_15 (not_15_out, OP5);
  not not_16 (not_16_out, OP3);
  not not_17 (not_17_out, OP2);
  not not_18 (not_18_out, OP0);
  not not_19 (not_19_out, IsFunct);
  not not_20 (not_20_out, OP5);
  not not_21 (not_21_out, OP2);
  not not_22 (not_22_out, OP1);
  not not_23 (not_23_out, IsFunct);
  not not_24 (not_24_out, OP5);
  not not_25 (not_25_out, OP3);
  not not_26 (not_26_out, OP1);
  not not_27 (not_27_out, OP5);
  not not_28 (not_28_out, OP2);
  not not_29 (not_29_out, IsFunct);
  not not_30 (not_30_out, OP5);
  not not_31 (not_31_out, OP3);
  not not_32 (not_32_out, OP3);
  and and_1 (and_1_out, not_1_out, not_2_out, not_3_out);
  and and_2 (and_2_out, not_4_out, not_5_out, OP2, not_6_out);
  and and_3 (and_3_out, IsFunct, OP5, OP2);
  and and_4 (and_4_out, OP1, not_7_out);
  and and_5 (and_5_out, IsFunct, OP1);
  and and_6 (and_6_out, not_8_out, not_9_out, not_10_out);
  and and_7 (and_7_out, not_11_out, not_12_out);
  and and_8 (and_8_out, OP3, OP0);
  and and_9 (and_9_out, OP5, OP0);
  and and_10 (and_10_out, not_13_out, not_14_out);
  and and_11 (and_11_out, not_15_out, not_16_out, OP0);
  and and_12 (IsSignedSLT, OP3, not_17_out, OP1, not_18_out);
  and and_13 (and_13_out, not_19_out, not_20_out, not_21_out, OP1, OP0);
  and and_14 (and_14_out, IsFunct, OP3, OP0);
  and and_15 (JumpReg, IsFunct, OP3, not_22_out);
  and and_16 (and_16_out, not_23_out, not_24_out, not_25_out);
  and and_17 (and_17_out, IsFunct, OP3, not_26_out);
  and and_18 (and_18_out, not_27_out, not_28_out, OP0);
  and and_19 (and_19_out, not_29_out, not_30_out, OP3);
  and and_20 (and_20_out, OP5, not_31_out);
  and and_21 (and_21_out, IsFunct, not_32_out);
  and and_22 (and_22_out, IsFunct, OP1);
  or or_1 (ALUOp3, and_1_out, and_2_out, and_3_out);
  or or_2 (ALUOp2, and_4_out, and_5_out);
  or or_3 (ALUOp1, and_6_out, and_7_out, and_8_out, and_9_out);
  or or_4 (ALUOp0, and_10_out, and_11_out);
  or or_5 (IsUnsignedSLT, and_13_out, and_14_out);
  or or_6 (PCtoReg, and_16_out, and_17_out);
  or or_7 (RegWrite, and_18_out, and_19_out, and_20_out, and_21_out, and_22_out);

  assign RegShifter = OP2;
endmodule
